// Logisim project PRESENT.circ as structural Verilog: 16 circuits, main circuit main
module main (
  input  in_1,
  input  in_2,
  input  in_3,
  input  in_4,
  input  in_5,
  input  in_6,
  input  in_7,
  input  in_8,
  input  in_9,
  input  in_10,
  input  in_11,
  input  in_12,
  input  in_13,
  input  in_14,
  input  in_15,
  input  in_16,
  input  in_17,
  input  in_18,
  input  in_19,
  input  in_20,
  input  in_21,
  input  in_22,
  input  in_23,
  input  in_24,
  input  in_25,
  input  in_26,
  input  in_27,
  input  in_28,
  input  in_29,
  input  in_30,
  input  in_31,
  input  in_32,
  input  in_33,
  input  in_34,
  input  in_35,
  input  in_36,
  input  in_37,
  input  in_38,
  input  in_39,
  input  in_40,
  input  in_41,
  input  in_42,
  input  in_43,
  input  in_44,
  input  in_45,
  input  in_46,
  input  in_47,
  input  in_48,
  input  in_49,
  input  in_50,
  input  in_51,
  input  in_52,
  input  in_53,
  input  in_54,
  input  in_55,
  input  in_56,
  input  in_57,
  input  in_58,
  input  in_59,
  input  in_60,
  input  in_61,
  input  in_62,
  input  in_63,
  input  in_64
);

  Clock clock_1 ();  // open: out

  // Notes on the sheet:
  //   Main Clock
endmodule

module SBoxA (
  input  in_1,
  input  in_2,
  input  in_3,
  input  in_4,
  output out_5
);

  wire and_1_out, and_2_out, and_3_out, and_4_out, and_5_out, not_1_out, not_2_out, not_3_out, not_4_out;

  not not_1 (not_1_out, in_1);
  not not_2 (not_2_out, in_2);
  not not_3 (not_3_out, in_3);
  not not_4 (not_4_out, in_4);
  and and_1 (and_1_out, not_1_out, not_3_out, not_4_out);
  and and_2 (and_2_out, not_1_out, in_3, in_4);
  and and_3 (and_3_out, not_1_out, in_2, not_4_out);
  and and_4 (and_4_out, in_1, not_2_out, in_4);
  and and_5 (and_5_out, in_1, not_2_out, in_3);
  or or_1 (out_5, and_5_out, and_1_out, and_2_out, and_3_out, and_4_out);
endmodule

module SBoxB (
  input  in_1,
  input  in_2,
  input  in_3,
  input  in_4,
  output out_5
);

  wire and_1_out, and_2_out, and_3_out, and_4_out, and_5_out, not_1_out, not_2_out, not_3_out, not_4_out;

  not not_1 (not_1_out, in_1);
  not not_2 (not_2_out, in_2);
  not not_3 (not_3_out, in_3);
  not not_4 (not_4_out, in_4);
  and and_1 (and_1_out, not_1_out, not_2_out, not_3_out);
  and and_2 (and_2_out, not_2_out, not_3_out, in_4);
  and and_3 (and_3_out, not_2_out, in_3, not_4_out);
  and and_4 (and_4_out, in_1, in_1, in_2, not_3_out);
  and and_5 (and_5_out, not_1_out, in_2, in_3, in_4);
  or or_1 (out_5, and_5_out, and_1_out, and_2_out, and_3_out, and_4_out);
endmodule

module SBoxC (
  input  in_1,
  input  in_2,
  input  in_3,
  input  in_4,
  output out_5
);

  wire and_1_out, and_2_out, and_3_out, and_4_out, and_5_out, not_1_out, not_2_out, not_3_out, not_4_out;

  not not_1 (not_1_out, in_1);
  not not_2 (not_2_out, in_2);
  not not_3 (not_3_out, in_3);
  not not_4 (not_4_out, in_4);
  and and_1 (and_1_out, not_1_out, not_2_out, not_2_out, in_3);
  and and_2 (and_2_out, not_1_out, in_3, not_4_out);
  and and_3 (and_3_out, not_2_out, in_3, not_4_out);
  and and_4 (and_4_out, in_1, in_1, not_2_out, not_3_out);
  and and_5 (and_5_out, in_1, in_2, in_4);
  or or_1 (out_5, and_5_out, and_1_out, and_2_out, and_3_out, and_4_out);
endmodule

module SBoxD (
  input  in_1,
  input  in_2,
  input  in_3,
  input  in_4,
  output out_5
);

  wire and_1_out, and_2_out, and_3_out, and_4_out, and_5_out, and_6_out, not_1_out, not_2_out, not_3_out,
       not_4_out, or_1_out;

  not not_1 (not_1_out, in_1);
  not not_2 (not_2_out, in_2);
  not not_3 (not_3_out, in_3);
  not not_4 (not_4_out, in_4);
  and and_1 (and_1_out, not_1_out, not_2_out, in_4, in_4);
  and and_2 (and_2_out, not_1_out, in_3, in_4);
  and and_3 (and_3_out, in_1, not_2_out, not_4_out);
  and and_4 (and_4_out, in_1, in_3, not_4_out);
  and and_5 (and_5_out, not_1_out, in_2, not_3_out, not_4_out);
  and and_6 (and_6_out, in_1, in_2, not_3_out, in_4);
  or or_1 (or_1_out, and_5_out, and_6_out);
  or or_2 (out_5, or_1_out, and_1_out, and_2_out, and_3_out, and_4_out);
endmodule

module SBox4Bit (
  input  in_1,
  input  in_2,
  input  in_3,
  input  in_4,
  output out_5,
  output out_6,
  output out_7,
  output out_8
);

  SBoxA sboxa_1 (.in_1(in_1), .in_2(in_2), .in_3(in_3), .in_4(in_4), .out_5(out_5));
  SBoxB sboxb_1 (.in_1(in_1), .in_2(in_2), .in_3(in_3), .in_4(in_4), .out_5(out_6));
  SBoxC sboxc_1 (.in_1(in_1), .in_2(in_2), .in_3(in_3), .in_4(in_4), .out_5(out_7));
  SBoxD sboxd_1 (.in_1(in_1), .in_2(in_2), .in_3(in_3), .in_4(in_4), .out_5(out_8));
endmodule

module Sbox64Bit (
  input  in_1,
  input  in_2,
  input  in_3,
  input  in_4,
  input  in_5,
  input  in_6,
  input  in_7,
  input  in_8,
  input  in_9,
  input  in_10,
  input  in_11,
  input  in_12,
  input  in_13,
  input  in_14,
  input  in_15,
  input  in_16,
  input  in_17,
  input  in_18,
  input  in_19,
  input  in_20,
  input  in_21,
  input  in_22,
  input  in_23,
  input  in_24,
  input  in_25,
  input  in_26,
  input  in_27,
  input  in_28,
  input  in_29,
  input  in_30,
  input  in_31,
  input  in_32,
  input  in_33,
  input  in_34,
  input  in_35,
  input  in_36,
  input  in_37,
  input  in_38,
  input  in_39,
  input  in_40,
  input  in_41,
  input  in_42,
  input  in_43,
  input  in_44,
  input  in_45,
  input  in_46,
  input  in_47,
  input  in_48,
  input  in_49,
  input  in_50,
  input  in_51,
  input  in_52,
  input  in_53,
  input  in_54,
  input  in_55,
  input  in_56,
  input  in_57,
  input  in_58,
  input  in_59,
  input  in_60,
  input  in_61,
  input  in_62,
  input  in_63,
  input  in_64,
  output out_65,
  output out_66,
  output out_67,
  output out_68,
  output out_69,
  output out_70,
  output out_71,
  output out_72,
  output out_73,
  output out_74,
  output out_75,
  output out_76,
  output out_77,
  output out_78,
  output out_79,
  output out_80,
  output out_81,
  output out_82,
  output out_83,
  output out_84,
  output out_85,
  output out_86,
  output out_87,
  output out_88,
  output out_89,
  output out_90,
  output out_91,
  output out_92,
  output out_93,
  output out_94,
  output out_95,
  output out_96,
  output out_97,
  output out_98,
  output out_99,
  output out_100,
  output out_101,
  output out_102,
  output out_103,
  output out_104,
  output out_105,
  output out_106,
  output out_107,
  output out_108,
  output out_109,
  output out_110,
  output out_111,
  output out_112,
  output out_113,
  output out_114,
  output out_115,
  output out_116,
  output out_117,
  output out_118,
  output out_119,
  output out_120,
  output out_121,
  output out_122,
  output out_123,
  output out_124,
  output out_125,
  output out_126,
  output out_127,
  output out_128
);

  SBox4Bit sbox4bit_1 (
    .in_1(in_1), .in_2(in_2), .in_3(in_3), .in_4(in_4), .out_5(out_65), .out_6(out_66), .out_7(out_67),
    .out_8(out_68));
  SBox4Bit sbox4bit_2 (
    .in_1(in_5), .in_2(in_6), .in_3(in_7), .in_4(in_8), .out_5(out_69), .out_6(out_70), .out_7(out_71),
    .out_8(out_72));
  SBox4Bit sbox4bit_3 (
    .in_1(in_9), .in_2(in_10), .in_3(in_11), .in_4(in_12), .out_5(out_73), .out_6(out_74), .out_7(out_75),
    .out_8(out_76));
  SBox4Bit sbox4bit_4 (
    .in_1(in_13), .in_2(in_14), .in_3(in_15), .in_4(in_16), .out_5(out_77), .out_6(out_78), .out_7(out_79),
    .out_8(out_80));
  SBox4Bit sbox4bit_5 (
    .in_1(in_17), .in_2(in_18), .in_3(in_19), .in_4(in_20), .out_5(out_81), .out_6(out_82), .out_7(out_83),
    .out_8(out_84));
  SBox4Bit sbox4bit_6 (
    .in_1(in_21), .in_2(in_22), .in_3(in_23), .in_4(in_24), .out_5(out_85), .out_6(out_86), .out_7(out_87),
    .out_8(out_88));
  SBox4Bit sbox4bit_7 (
    .in_1(in_25), .in_2(in_26), .in_3(in_27), .in_4(in_28), .out_5(out_89), .out_6(out_90), .out_7(out_91),
    .out_8(out_92));
  SBox4Bit sbox4bit_8 (
    .in_1(in_29), .in_2(in_30), .in_3(in_31), .in_4(in_32), .out_5(out_93), .out_6(out_94), .out_7(out_95),
    .out_8(out_96));
  SBox4Bit sbox4bit_9 (
    .in_1(in_33), .in_2(in_34), .in_3(in_35), .in_4(in_36), .out_5(out_97), .out_6(out_98), .out_7(out_99),
    .out_8(out_100));
  SBox4Bit sbox4bit_10 (
    .in_1(in_37), .in_2(in_38), .in_3(in_39), .in_4(in_40), .out_5(out_101), .out_6(out_102),
    .out_7(out_103), .out_8(out_104));
  SBox4Bit sbox4bit_11 (
    .in_1(in_41), .in_2(in_42), .in_3(in_43), .in_4(in_44), .out_5(out_105), .out_6(out_106),
    .out_7(out_107), .out_8(out_108));
  SBox4Bit sbox4bit_12 (
    .in_1(in_45), .in_2(in_46), .in_3(in_47), .in_4(in_48), .out_5(out_109), .out_6(out_110),
    .out_7(out_111), .out_8(out_112));
  SBox4Bit sbox4bit_13 (
    .in_1(in_49), .in_2(in_50), .in_3(in_51), .in_4(in_52), .out_5(out_113), .out_6(out_114),
    .out_7(out_115), .out_8(out_116));
  SBox4Bit sbox4bit_14 (
    .in_1(in_53), .in_2(in_54), .in_3(in_55), .in_4(in_56), .out_5(out_117), .out_6(out_118),
    .out_7(out_119), .out_8(out_120));
  SBox4Bit sbox4bit_15 (
    .in_1(in_57), .in_2(in_58), .in_3(in_59), .in_4(in_60), .out_5(out_121), .out_6(out_122),
    .out_7(out_123), .out_8(out_124));
  SBox4Bit sbox4bit_16 (
    .in_1(in_61), .in_2(in_62), .in_3(in_63), .in_4(in_64), .out_5(out_125), .out_6(out_126),
    .out_7(out_127), .out_8(out_128));
endmodule

module XOR4 (
  input  in_1,
  input  in_2,
  input  in_3,
  input  in_4,
  input  in_5,
  input  in_6,
  input  in_7,
  input  in_8,
  output out_9,
  output out_10,
  output out_11,
  output out_12
);

  xor xor_1 (out_9, in_1, in_5);
  xor xor_2 (out_10, in_2, in_6);
  xor xor_3 (out_11, in_3, in_7);
  xor xor_4 (out_12, in_4, in_8);
endmodule

module XOR16 (
  input  in_1,
  input  in_2,
  input  in_3,
  input  in_4,
  input  in_5,
  input  in_6,
  input  in_7,
  input  in_8,
  input  in_9,
  input  in_10,
  input  in_11,
  input  in_12,
  input  in_13,
  input  in_14,
  input  in_15,
  input  in_16,
  input  in_17,
  input  in_18,
  input  in_19,
  input  in_20,
  input  in_21,
  input  in_22,
  input  in_23,
  input  in_24,
  input  in_25,
  input  in_26,
  input  in_27,
  input  in_28,
  input  in_29,
  input  in_30,
  input  in_31,
  input  in_32,
  output out_33,
  output out_34,
  output out_35,
  output out_36,
  output out_37,
  output out_38,
  output out_39,
  output out_40,
  output out_41,
  output out_42,
  output out_43,
  output out_44,
  output out_45,
  output out_46,
  output out_47,
  output out_48
);

  XOR4 xor4_1 (
    .in_1(in_1), .in_2(in_2), .in_3(in_3), .in_4(in_4), .in_5(in_17), .in_6(in_18), .in_7(in_19),
    .in_8(in_20), .out_9(out_33), .out_10(out_34), .out_11(out_35), .out_12(out_36));
  XOR4 xor4_2 (
    .in_1(in_5), .in_2(in_6), .in_3(in_7), .in_4(in_8), .in_5(in_21), .in_6(in_22), .in_7(in_23),
    .in_8(in_24), .out_9(out_37), .out_10(out_38), .out_11(out_39), .out_12(out_40));
  XOR4 xor4_3 (
    .in_1(in_9), .in_2(in_10), .in_3(in_11), .in_4(in_12), .in_5(in_25), .in_6(in_26), .in_7(in_27),
    .in_8(in_28), .out_9(out_41), .out_10(out_42), .out_11(out_43), .out_12(out_44));
  XOR4 xor4_4 (
    .in_1(in_13), .in_2(in_14), .in_3(in_15), .in_4(in_16), .in_5(in_29), .in_6(in_30), .in_7(in_31),
    .in_8(in_32), .out_9(out_45), .out_10(out_46), .out_11(out_47), .out_12(out_48));
endmodule

module AddRoundKey (
  input  in_1,
  input  in_2,
  input  in_3,
  input  in_4,
  input  in_5,
  input  in_6,
  input  in_7,
  input  in_8,
  input  in_9,
  input  in_10,
  input  in_11,
  input  in_12,
  input  in_13,
  input  in_14,
  input  in_15,
  input  in_16,
  input  in_17,
  input  in_18,
  input  in_19,
  input  in_20,
  input  in_21,
  input  in_22,
  input  in_23,
  input  in_24,
  input  in_25,
  input  in_26,
  input  in_27,
  input  in_28,
  input  in_29,
  input  in_30,
  input  in_31,
  input  in_32,
  input  in_33,
  input  in_34,
  input  in_35,
  input  in_36,
  input  in_37,
  input  in_38,
  input  in_39,
  input  in_40,
  input  in_41,
  input  in_42,
  input  in_43,
  input  in_44,
  input  in_45,
  input  in_46,
  input  in_47,
  input  in_48,
  input  in_49,
  input  in_50,
  input  in_51,
  input  in_52,
  input  in_53,
  input  in_54,
  input  in_55,
  input  in_56,
  input  in_57,
  input  in_58,
  input  in_59,
  input  in_60,
  input  in_61,
  input  in_62,
  input  in_63,
  input  in_64,
  input  in_65,
  input  in_66,
  input  in_67,
  input  in_68,
  input  in_69,
  input  in_70,
  input  in_71,
  input  in_72,
  input  in_73,
  input  in_74,
  input  in_75,
  input  in_76,
  input  in_77,
  input  in_78,
  input  in_79,
  input  in_80,
  input  in_81,
  input  in_82,
  input  in_83,
  input  in_84,
  input  in_85,
  input  in_86,
  input  in_87,
  input  in_88,
  input  in_89,
  input  in_90,
  input  in_91,
  input  in_92,
  input  in_93,
  input  in_94,
  input  in_95,
  input  in_96,
  input  in_97,
  input  in_98,
  input  in_99,
  input  in_100,
  input  in_101,
  input  in_102,
  input  in_103,
  input  in_104,
  input  in_105,
  input  in_106,
  input  in_107,
  input  in_108,
  input  in_109,
  input  in_110,
  input  in_111,
  input  in_112,
  input  in_113,
  input  in_114,
  input  in_115,
  input  in_116,
  input  in_117,
  input  in_118,
  input  in_119,
  input  in_120,
  input  in_121,
  input  in_122,
  input  in_123,
  input  in_124,
  input  in_125,
  input  in_126,
  input  in_127,
  input  in_128,
  output out_129,
  output out_130,
  output out_131,
  output out_132,
  output out_133,
  output out_134,
  output out_135,
  output out_136,
  output out_137,
  output out_138,
  output out_139,
  output out_140,
  output out_141,
  output out_142,
  output out_143,
  output out_144,
  output out_145,
  output out_146,
  output out_147,
  output out_148,
  output out_149,
  output out_150,
  output out_151,
  output out_152,
  output out_153,
  output out_154,
  output out_155,
  output out_156,
  output out_157,
  output out_158,
  output out_159,
  output out_160,
  output out_161,
  output out_162,
  output out_163,
  output out_164,
  output out_165,
  output out_166,
  output out_167,
  output out_168,
  output out_169,
  output out_170,
  output out_171,
  output out_172,
  output out_173,
  output out_174,
  output out_175,
  output out_176,
  output out_177,
  output out_178,
  output out_179,
  output out_180,
  output out_181,
  output out_182,
  output out_183,
  output out_184,
  output out_185,
  output out_186,
  output out_187,
  output out_188,
  output out_189,
  output out_190,
  output out_191,
  output out_192
);

  XOR16 xor16_1 (
    .in_1(in_1), .in_2(in_2), .in_3(in_3), .in_4(in_4), .in_5(in_5), .in_6(in_6), .in_7(in_7), .in_8(in_8),
    .in_9(in_9), .in_10(in_10), .in_11(in_11), .in_12(in_12), .in_13(in_13), .in_14(in_14), .in_15(in_15),
    .in_16(in_16), .in_17(in_65), .in_18(in_66), .in_19(in_67), .in_20(in_68), .in_21(in_69), .in_22(in_70),
    .in_23(in_71), .in_24(in_72), .in_25(in_73), .in_26(in_74), .in_27(in_75), .in_28(in_76), .in_29(in_77),
    .in_30(in_78), .in_31(in_79), .in_32(in_80), .out_33(out_129), .out_34(out_130), .out_35(out_131),
    .out_36(out_132), .out_37(out_133), .out_38(out_134), .out_39(out_135), .out_40(out_136),
    .out_41(out_137), .out_42(out_138), .out_43(out_139), .out_44(out_140), .out_45(out_141),
    .out_46(out_142), .out_47(out_143), .out_48(out_144));
  XOR16 xor16_2 (
    .in_1(in_17), .in_2(in_18), .in_3(in_19), .in_4(in_20), .in_5(in_21), .in_6(in_22), .in_7(in_23),
    .in_8(in_24), .in_9(in_25), .in_10(in_26), .in_11(in_27), .in_12(in_28), .in_13(in_29), .in_14(in_30),
    .in_15(in_31), .in_16(in_32), .in_17(in_81), .in_18(in_82), .in_19(in_83), .in_20(in_84), .in_21(in_85),
    .in_22(in_86), .in_23(in_87), .in_24(in_88), .in_25(in_89), .in_26(in_90), .in_27(in_91), .in_28(in_92),
    .in_29(in_93), .in_30(in_94), .in_31(in_95), .in_32(in_96), .out_33(out_145), .out_34(out_146),
    .out_35(out_147), .out_36(out_148), .out_37(out_149), .out_38(out_150), .out_39(out_151),
    .out_40(out_152), .out_41(out_153), .out_42(out_154), .out_43(out_155), .out_44(out_156),
    .out_45(out_157), .out_46(out_158), .out_47(out_159), .out_48(out_160));
  XOR16 xor16_3 (
    .in_1(in_33), .in_2(in_34), .in_3(in_35), .in_4(in_36), .in_5(in_37), .in_6(in_38), .in_7(in_39),
    .in_8(in_40), .in_9(in_41), .in_10(in_42), .in_11(in_43), .in_12(in_44), .in_13(in_45), .in_14(in_46),
    .in_15(in_47), .in_16(in_48), .in_17(in_97), .in_18(in_98), .in_19(in_99), .in_20(in_100),
    .in_21(in_101), .in_22(in_102), .in_23(in_103), .in_24(in_104), .in_25(in_105), .in_26(in_106),
    .in_27(in_107), .in_28(in_108), .in_29(in_109), .in_30(in_110), .in_31(in_111), .in_32(in_112),
    .out_33(out_161), .out_34(out_162), .out_35(out_163), .out_36(out_164), .out_37(out_165),
    .out_38(out_166), .out_39(out_167), .out_40(out_168), .out_41(out_169), .out_42(out_170),
    .out_43(out_171), .out_44(out_172), .out_45(out_173), .out_46(out_174), .out_47(out_175), .out_48(out_176));
  XOR16 xor16_4 (
    .in_1(in_49), .in_2(in_50), .in_3(in_51), .in_4(in_52), .in_5(in_53), .in_6(in_54), .in_7(in_55),
    .in_8(in_56), .in_9(in_57), .in_10(in_58), .in_11(in_59), .in_12(in_60), .in_13(in_61), .in_14(in_62),
    .in_15(in_63), .in_16(in_64), .in_17(in_113), .in_18(in_114), .in_19(in_115), .in_20(in_116),
    .in_21(in_117), .in_22(in_118), .in_23(in_119), .in_24(in_120), .in_25(in_121), .in_26(in_122),
    .in_27(in_123), .in_28(in_124), .in_29(in_125), .in_30(in_126), .in_31(in_127), .in_32(in_128),
    .out_33(out_177), .out_34(out_178), .out_35(out_179), .out_36(out_180), .out_37(out_181),
    .out_38(out_182), .out_39(out_183), .out_40(out_184), .out_41(out_185), .out_42(out_186),
    .out_43(out_187), .out_44(out_188), .out_45(out_189), .out_46(out_190), .out_47(out_191), .out_48(out_192));
endmodule

module PBox (
  input  in_1,
  input  in_2,
  input  in_3,
  input  in_4,
  input  in_5,
  input  in_6,
  input  in_7,
  input  in_8,
  input  in_9,
  input  in_10,
  input  in_11,
  input  in_12,
  input  in_13,
  input  in_14,
  input  in_15,
  input  in_16,
  input  in_17,
  input  in_18,
  input  in_19,
  input  in_20,
  input  in_21,
  input  in_22,
  input  in_23,
  input  in_24,
  input  in_25,
  input  in_26,
  input  in_27,
  input  in_28,
  input  in_29,
  input  in_30,
  input  in_31,
  input  in_32,
  input  in_33,
  input  in_34,
  input  in_35,
  input  in_36,
  input  in_37,
  input  in_38,
  input  in_39,
  input  in_40,
  input  in_41,
  input  in_42,
  input  in_43,
  input  in_44,
  input  in_45,
  input  in_46,
  input  in_47,
  input  in_48,
  input  in_49,
  input  in_50,
  input  in_51,
  input  in_52,
  input  in_53,
  input  in_54,
  input  in_55,
  input  in_56,
  input  in_57,
  input  in_58,
  input  in_59,
  input  in_60,
  input  in_61,
  input  in_62,
  input  in_63,
  input  in_64,
  output out_65,
  output out_66,
  output out_67,
  output out_68,
  output out_69,
  output out_70,
  output out_71,
  output out_72,
  output out_73,
  output out_74,
  output out_75,
  output out_76,
  output out_77,
  output out_78,
  output out_79,
  output out_80,
  output out_81,
  output out_82,
  output out_83,
  output out_84,
  output out_85,
  output out_86,
  output out_87,
  output out_88,
  output out_89,
  output out_90,
  output out_91,
  output out_92,
  output out_93,
  output out_94,
  output out_95,
  output out_96,
  output out_97,
  output out_98,
  output out_99,
  output out_100,
  output out_101,
  output out_102,
  output out_103,
  output out_104,
  output out_105,
  output out_106,
  output out_107,
  output out_108,
  output out_109,
  output out_110,
  output out_111,
  output out_112,
  output out_113,
  output out_114,
  output out_115,
  output out_116,
  output out_117,
  output out_118,
  output out_119,
  output out_120,
  output out_121,
  output out_122,
  output out_123,
  output out_124,
  output out_125,
  output out_126,
  output out_127,
  output out_128
);


  assign out_65 = in_1;
  assign out_66 = in_5;
  assign out_67 = in_9;
  assign out_68 = in_13;
  assign out_69 = in_17;
  assign out_70 = in_21;
  assign out_71 = in_25;
  assign out_72 = in_29;
  assign out_73 = in_33;
  assign out_74 = in_37;
  assign out_75 = in_41;
  assign out_76 = in_45;
  assign out_77 = in_49;
  assign out_78 = in_53;
  assign out_79 = in_57;
  assign out_80 = in_61;
  assign out_81 = in_2;
  assign out_82 = in_6;
  assign out_83 = in_10;
  assign out_84 = in_14;
  assign out_85 = in_18;
  assign out_86 = in_22;
  assign out_87 = in_26;
  assign out_88 = in_30;
  assign out_89 = in_34;
  assign out_90 = in_38;
  assign out_91 = in_42;
  assign out_92 = in_46;
  assign out_93 = in_50;
  assign out_94 = in_54;
  assign out_95 = in_58;
  assign out_96 = in_62;
  assign out_97 = in_3;
  assign out_98 = in_7;
  assign out_99 = in_11;
  assign out_100 = in_15;
  assign out_101 = in_19;
  assign out_102 = in_23;
  assign out_103 = in_27;
  assign out_104 = in_31;
  assign out_105 = in_35;
  assign out_106 = in_39;
  assign out_107 = in_43;
  assign out_108 = in_47;
  assign out_109 = in_51;
  assign out_110 = in_55;
  assign out_111 = in_63;
  assign out_112 = in_59;
  assign out_113 = in_4;
  assign out_114 = in_8;
  assign out_115 = in_12;
  assign out_116 = in_16;
  assign out_117 = in_20;
  assign out_118 = in_24;
  assign out_119 = in_28;
  assign out_120 = in_32;
  assign out_121 = in_36;
  assign out_122 = in_40;
  assign out_123 = in_44;
  assign out_124 = in_48;
  assign out_125 = in_52;
  assign out_126 = in_56;
  assign out_127 = in_60;
  assign out_128 = in_64;
endmodule

module SPRLayer (
  input  in_1,
  input  in_2,
  input  in_3,
  input  in_4,
  input  in_5,
  input  in_6,
  input  in_7,
  input  in_8,
  input  in_9,
  input  in_10,
  input  in_11,
  input  in_12,
  input  in_13,
  input  in_14,
  input  in_15,
  input  in_16,
  input  in_17,
  input  in_18,
  input  in_19,
  input  in_20,
  input  in_21,
  input  in_22,
  input  in_23,
  input  in_24,
  input  in_25,
  input  in_26,
  input  in_27,
  input  in_28,
  input  in_29,
  input  in_30,
  input  in_31,
  input  in_32,
  input  in_33,
  input  in_34,
  input  in_35,
  input  in_36,
  input  in_37,
  input  in_38,
  input  in_39,
  input  in_40,
  input  in_41,
  input  in_42,
  input  in_43,
  input  in_44,
  input  in_45,
  input  in_46,
  input  in_47,
  input  in_48,
  input  in_49,
  input  in_50,
  input  in_51,
  input  in_52,
  input  in_53,
  input  in_54,
  input  in_55,
  input  in_56,
  input  in_57,
  input  in_58,
  input  in_59,
  input  in_60,
  input  in_61,
  input  in_62,
  input  in_63,
  input  in_64,
  input  in_65,
  input  in_66,
  input  in_67,
  input  in_68,
  input  in_69,
  input  in_70,
  input  in_71,
  input  in_72,
  input  in_73,
  input  in_74,
  input  in_75,
  input  in_76,
  input  in_77,
  input  in_78,
  input  in_79,
  input  in_80,
  input  in_81,
  input  in_82,
  input  in_83,
  input  in_84,
  input  in_85,
  input  in_86,
  input  in_87,
  input  in_88,
  input  in_89,
  input  in_90,
  input  in_91,
  input  in_92,
  input  in_93,
  input  in_94,
  input  in_95,
  input  in_96,
  input  in_97,
  input  in_98,
  input  in_99,
  input  in_100,
  input  in_101,
  input  in_102,
  input  in_103,
  input  in_104,
  input  in_105,
  input  in_106,
  input  in_107,
  input  in_108,
  input  in_109,
  input  in_110,
  input  in_111,
  input  in_112,
  input  in_113,
  input  in_114,
  input  in_115,
  input  in_116,
  input  in_117,
  input  in_118,
  input  in_119,
  input  in_120,
  input  in_121,
  input  in_122,
  input  in_123,
  input  in_124,
  input  in_125,
  input  in_126,
  input  in_127,
  input  in_128,
  output out_129,
  output out_130,
  output out_131,
  output out_132,
  output out_133,
  output out_134,
  output out_135,
  output out_136,
  output out_137,
  output out_138,
  output out_139,
  output out_140,
  output out_141,
  output out_142,
  output out_143,
  output out_144,
  output out_145,
  output out_146,
  output out_147,
  output out_148,
  output out_149,
  output out_150,
  output out_151,
  output out_152,
  output out_153,
  output out_154,
  output out_155,
  output out_156,
  output out_157,
  output out_158,
  output out_159,
  output out_160,
  output out_161,
  output out_162,
  output out_163,
  output out_164,
  output out_165,
  output out_166,
  output out_167,
  output out_168,
  output out_169,
  output out_170,
  output out_171,
  output out_172,
  output out_173,
  output out_174,
  output out_175,
  output out_176,
  output out_177,
  output out_178,
  output out_179,
  output out_180,
  output out_181,
  output out_182,
  output out_183,
  output out_184,
  output out_185,
  output out_186,
  output out_187,
  output out_188,
  output out_189,
  output out_190,
  output out_191,
  output out_192
);

  wire pbox_1_out_65, pbox_1_out_66, pbox_1_out_67, pbox_1_out_68, pbox_1_out_69, pbox_1_out_70,
       pbox_1_out_71, pbox_1_out_72, pbox_1_out_73, pbox_1_out_74, pbox_1_out_75, pbox_1_out_76,
       pbox_1_out_77, pbox_1_out_78, pbox_1_out_79, pbox_1_out_80, pbox_1_out_81, pbox_1_out_82,
       pbox_1_out_83, pbox_1_out_84, pbox_1_out_85, pbox_1_out_86, pbox_1_out_87, pbox_1_out_88,
       pbox_1_out_89, pbox_1_out_90, pbox_1_out_91, pbox_1_out_92, pbox_1_out_93, pbox_1_out_94,
       pbox_1_out_95, pbox_1_out_96, pbox_1_out_97, pbox_1_out_98, pbox_1_out_99, pbox_1_out_100,
       pbox_1_out_101, pbox_1_out_102, pbox_1_out_103, pbox_1_out_104, pbox_1_out_105, pbox_1_out_106,
       pbox_1_out_107, pbox_1_out_108, pbox_1_out_109, pbox_1_out_110, pbox_1_out_111, pbox_1_out_112,
       pbox_1_out_113, pbox_1_out_114, pbox_1_out_115, pbox_1_out_116, pbox_1_out_117, pbox_1_out_118,
       pbox_1_out_119, pbox_1_out_120, pbox_1_out_121, pbox_1_out_122, pbox_1_out_123, pbox_1_out_124,
       pbox_1_out_125, pbox_1_out_126, pbox_1_out_127, pbox_1_out_128, sbox64bit_1_out_65,
       sbox64bit_1_out_66, sbox64bit_1_out_67, sbox64bit_1_out_68, sbox64bit_1_out_69, sbox64bit_1_out_70,
       sbox64bit_1_out_71, sbox64bit_1_out_72, sbox64bit_1_out_73, sbox64bit_1_out_74, sbox64bit_1_out_75,
       sbox64bit_1_out_76, sbox64bit_1_out_77, sbox64bit_1_out_78, sbox64bit_1_out_79, sbox64bit_1_out_80,
       sbox64bit_1_out_81, sbox64bit_1_out_82, sbox64bit_1_out_83, sbox64bit_1_out_84, sbox64bit_1_out_85,
       sbox64bit_1_out_86, sbox64bit_1_out_87, sbox64bit_1_out_88, sbox64bit_1_out_89, sbox64bit_1_out_90,
       sbox64bit_1_out_91, sbox64bit_1_out_92, sbox64bit_1_out_93, sbox64bit_1_out_94, sbox64bit_1_out_95,
       sbox64bit_1_out_96, sbox64bit_1_out_97, sbox64bit_1_out_98, sbox64bit_1_out_99, sbox64bit_1_out_100,
       sbox64bit_1_out_101, sbox64bit_1_out_102, sbox64bit_1_out_103, sbox64bit_1_out_104,
       sbox64bit_1_out_105, sbox64bit_1_out_106, sbox64bit_1_out_107, sbox64bit_1_out_108,
       sbox64bit_1_out_109, sbox64bit_1_out_110, sbox64bit_1_out_111, sbox64bit_1_out_112,
       sbox64bit_1_out_113, sbox64bit_1_out_114, sbox64bit_1_out_115, sbox64bit_1_out_116,
       sbox64bit_1_out_117, sbox64bit_1_out_118, sbox64bit_1_out_119, sbox64bit_1_out_120,
       sbox64bit_1_out_121, sbox64bit_1_out_122, sbox64bit_1_out_123, sbox64bit_1_out_124,
       sbox64bit_1_out_125, sbox64bit_1_out_126, sbox64bit_1_out_127, sbox64bit_1_out_128;

  Sbox64Bit sbox64bit_1 (
    .in_1(in_65), .in_2(in_66), .in_3(in_67), .in_4(in_68), .in_5(in_69), .in_6(in_70), .in_7(in_71),
    .in_8(in_72), .in_9(in_73), .in_10(in_74), .in_11(in_75), .in_12(in_76), .in_13(in_77), .in_14(in_78),
    .in_15(in_79), .in_16(in_80), .in_17(in_81), .in_18(in_82), .in_19(in_83), .in_20(in_84), .in_21(in_85),
    .in_22(in_86), .in_23(in_87), .in_24(in_88), .in_25(in_89), .in_26(in_90), .in_27(in_91), .in_28(in_92),
    .in_29(in_93), .in_30(in_94), .in_31(in_95), .in_32(in_96), .in_33(in_97), .in_34(in_98), .in_35(in_99),
    .in_36(in_100), .in_37(in_101), .in_38(in_102), .in_39(in_103), .in_40(in_104), .in_41(in_105),
    .in_42(in_106), .in_43(in_107), .in_44(in_108), .in_45(in_109), .in_46(in_110), .in_47(in_111),
    .in_48(in_112), .in_49(in_113), .in_50(in_114), .in_51(in_115), .in_52(in_116), .in_53(in_117),
    .in_54(in_118), .in_55(in_119), .in_56(in_120), .in_57(in_121), .in_58(in_122), .in_59(in_123),
    .in_60(in_124), .in_61(in_125), .in_62(in_126), .in_63(in_127), .in_64(in_128),
    .out_65(sbox64bit_1_out_65), .out_66(sbox64bit_1_out_66), .out_67(sbox64bit_1_out_67),
    .out_68(sbox64bit_1_out_68), .out_69(sbox64bit_1_out_69), .out_70(sbox64bit_1_out_70),
    .out_71(sbox64bit_1_out_71), .out_72(sbox64bit_1_out_72), .out_73(sbox64bit_1_out_73),
    .out_74(sbox64bit_1_out_74), .out_75(sbox64bit_1_out_75), .out_76(sbox64bit_1_out_76),
    .out_77(sbox64bit_1_out_77), .out_78(sbox64bit_1_out_78), .out_79(sbox64bit_1_out_79),
    .out_80(sbox64bit_1_out_80), .out_81(sbox64bit_1_out_81), .out_82(sbox64bit_1_out_82),
    .out_83(sbox64bit_1_out_83), .out_84(sbox64bit_1_out_84), .out_85(sbox64bit_1_out_85),
    .out_86(sbox64bit_1_out_86), .out_87(sbox64bit_1_out_87), .out_88(sbox64bit_1_out_88),
    .out_89(sbox64bit_1_out_89), .out_90(sbox64bit_1_out_90), .out_91(sbox64bit_1_out_91),
    .out_92(sbox64bit_1_out_92), .out_93(sbox64bit_1_out_93), .out_94(sbox64bit_1_out_94),
    .out_95(sbox64bit_1_out_95), .out_96(sbox64bit_1_out_96), .out_97(sbox64bit_1_out_97),
    .out_98(sbox64bit_1_out_98), .out_99(sbox64bit_1_out_99), .out_100(sbox64bit_1_out_100),
    .out_101(sbox64bit_1_out_101), .out_102(sbox64bit_1_out_102), .out_103(sbox64bit_1_out_103),
    .out_104(sbox64bit_1_out_104), .out_105(sbox64bit_1_out_105), .out_106(sbox64bit_1_out_106),
    .out_107(sbox64bit_1_out_107), .out_108(sbox64bit_1_out_108), .out_109(sbox64bit_1_out_109),
    .out_110(sbox64bit_1_out_110), .out_111(sbox64bit_1_out_111), .out_112(sbox64bit_1_out_112),
    .out_113(sbox64bit_1_out_113), .out_114(sbox64bit_1_out_114), .out_115(sbox64bit_1_out_115),
    .out_116(sbox64bit_1_out_116), .out_117(sbox64bit_1_out_117), .out_118(sbox64bit_1_out_118),
    .out_119(sbox64bit_1_out_119), .out_120(sbox64bit_1_out_120), .out_121(sbox64bit_1_out_121),
    .out_122(sbox64bit_1_out_122), .out_123(sbox64bit_1_out_123), .out_124(sbox64bit_1_out_124),
    .out_125(sbox64bit_1_out_125), .out_126(sbox64bit_1_out_126), .out_127(sbox64bit_1_out_127),
    .out_128(sbox64bit_1_out_128));
  PBox pbox_1 (
    .in_1(sbox64bit_1_out_65), .in_2(sbox64bit_1_out_66), .in_3(sbox64bit_1_out_67),
    .in_4(sbox64bit_1_out_68), .in_5(sbox64bit_1_out_69), .in_6(sbox64bit_1_out_70),
    .in_7(sbox64bit_1_out_71), .in_8(sbox64bit_1_out_72), .in_9(sbox64bit_1_out_73),
    .in_10(sbox64bit_1_out_74), .in_11(sbox64bit_1_out_75), .in_12(sbox64bit_1_out_76),
    .in_13(sbox64bit_1_out_77), .in_14(sbox64bit_1_out_78), .in_15(sbox64bit_1_out_79),
    .in_16(sbox64bit_1_out_80), .in_17(sbox64bit_1_out_81), .in_18(sbox64bit_1_out_82),
    .in_19(sbox64bit_1_out_83), .in_20(sbox64bit_1_out_84), .in_21(sbox64bit_1_out_85),
    .in_22(sbox64bit_1_out_86), .in_23(sbox64bit_1_out_87), .in_24(sbox64bit_1_out_88),
    .in_25(sbox64bit_1_out_89), .in_26(sbox64bit_1_out_90), .in_27(sbox64bit_1_out_91),
    .in_28(sbox64bit_1_out_92), .in_29(sbox64bit_1_out_93), .in_30(sbox64bit_1_out_94),
    .in_31(sbox64bit_1_out_95), .in_32(sbox64bit_1_out_96), .in_33(sbox64bit_1_out_97),
    .in_34(sbox64bit_1_out_98), .in_35(sbox64bit_1_out_99), .in_36(sbox64bit_1_out_100),
    .in_37(sbox64bit_1_out_101), .in_38(sbox64bit_1_out_102), .in_39(sbox64bit_1_out_103),
    .in_40(sbox64bit_1_out_104), .in_41(sbox64bit_1_out_105), .in_42(sbox64bit_1_out_106),
    .in_43(sbox64bit_1_out_107), .in_44(sbox64bit_1_out_108), .in_45(sbox64bit_1_out_109),
    .in_46(sbox64bit_1_out_110), .in_47(sbox64bit_1_out_111), .in_48(sbox64bit_1_out_112),
    .in_49(sbox64bit_1_out_113), .in_50(sbox64bit_1_out_114), .in_51(sbox64bit_1_out_115),
    .in_52(sbox64bit_1_out_116), .in_53(sbox64bit_1_out_117), .in_54(sbox64bit_1_out_118),
    .in_55(sbox64bit_1_out_119), .in_56(sbox64bit_1_out_120), .in_57(sbox64bit_1_out_121),
    .in_58(sbox64bit_1_out_122), .in_59(sbox64bit_1_out_123), .in_60(sbox64bit_1_out_124),
    .in_61(sbox64bit_1_out_125), .in_62(sbox64bit_1_out_126), .in_63(sbox64bit_1_out_127),
    .in_64(sbox64bit_1_out_128), .out_65(pbox_1_out_65), .out_66(pbox_1_out_66), .out_67(pbox_1_out_67),
    .out_68(pbox_1_out_68), .out_69(pbox_1_out_69), .out_70(pbox_1_out_70), .out_71(pbox_1_out_71),
    .out_72(pbox_1_out_72), .out_73(pbox_1_out_73), .out_74(pbox_1_out_74), .out_75(pbox_1_out_75),
    .out_76(pbox_1_out_76), .out_77(pbox_1_out_77), .out_78(pbox_1_out_78), .out_79(pbox_1_out_79),
    .out_80(pbox_1_out_80), .out_81(pbox_1_out_81), .out_82(pbox_1_out_82), .out_83(pbox_1_out_83),
    .out_84(pbox_1_out_84), .out_85(pbox_1_out_85), .out_86(pbox_1_out_86), .out_87(pbox_1_out_87),
    .out_88(pbox_1_out_88), .out_89(pbox_1_out_89), .out_90(pbox_1_out_90), .out_91(pbox_1_out_91),
    .out_92(pbox_1_out_92), .out_93(pbox_1_out_93), .out_94(pbox_1_out_94), .out_95(pbox_1_out_95),
    .out_96(pbox_1_out_96), .out_97(pbox_1_out_97), .out_98(pbox_1_out_98), .out_99(pbox_1_out_99),
    .out_100(pbox_1_out_100), .out_101(pbox_1_out_101), .out_102(pbox_1_out_102), .out_103(pbox_1_out_103),
    .out_104(pbox_1_out_104), .out_105(pbox_1_out_105), .out_106(pbox_1_out_106), .out_107(pbox_1_out_107),
    .out_108(pbox_1_out_108), .out_109(pbox_1_out_109), .out_110(pbox_1_out_110), .out_111(pbox_1_out_111),
    .out_112(pbox_1_out_112), .out_113(pbox_1_out_113), .out_114(pbox_1_out_114), .out_115(pbox_1_out_115),
    .out_116(pbox_1_out_116), .out_117(pbox_1_out_117), .out_118(pbox_1_out_118), .out_119(pbox_1_out_119),
    .out_120(pbox_1_out_120), .out_121(pbox_1_out_121), .out_122(pbox_1_out_122), .out_123(pbox_1_out_123),
    .out_124(pbox_1_out_124), .out_125(pbox_1_out_125), .out_126(pbox_1_out_126), .out_127(pbox_1_out_127),
    .out_128(pbox_1_out_128));
  AddRoundKey addroundkey_1 (
    .in_1(in_1), .in_2(in_2), .in_3(in_3), .in_4(in_4), .in_5(in_5), .in_6(in_6), .in_7(in_7), .in_8(in_8),
    .in_9(in_9), .in_10(in_10), .in_11(in_11), .in_12(in_12), .in_13(in_13), .in_14(in_14), .in_15(in_15),
    .in_16(in_16), .in_17(in_17), .in_18(in_18), .in_19(in_19), .in_20(in_20), .in_21(in_21), .in_22(in_22),
    .in_23(in_23), .in_24(in_24), .in_25(in_25), .in_26(in_26), .in_27(in_27), .in_28(in_28), .in_29(in_29),
    .in_30(in_30), .in_31(in_31), .in_32(in_32), .in_33(in_33), .in_34(in_34), .in_35(in_35), .in_36(in_36),
    .in_37(in_37), .in_38(in_38), .in_39(in_39), .in_40(in_40), .in_41(in_41), .in_42(in_42), .in_43(in_43),
    .in_44(in_44), .in_45(in_45), .in_46(in_46), .in_47(in_47), .in_48(in_48), .in_49(in_49), .in_50(in_50),
    .in_51(in_51), .in_52(in_52), .in_53(in_53), .in_54(in_54), .in_55(in_55), .in_56(in_56), .in_57(in_57),
    .in_58(in_58), .in_59(in_59), .in_60(in_60), .in_61(in_61), .in_62(in_62), .in_63(in_63), .in_64(in_64),
    .in_65(pbox_1_out_65), .in_66(pbox_1_out_66), .in_67(pbox_1_out_67), .in_68(pbox_1_out_68),
    .in_69(pbox_1_out_69), .in_70(pbox_1_out_70), .in_71(pbox_1_out_71), .in_72(pbox_1_out_72),
    .in_73(pbox_1_out_73), .in_74(pbox_1_out_74), .in_75(pbox_1_out_75), .in_76(pbox_1_out_76),
    .in_77(pbox_1_out_77), .in_78(pbox_1_out_78), .in_79(pbox_1_out_79), .in_80(pbox_1_out_80),
    .in_81(pbox_1_out_81), .in_82(pbox_1_out_82), .in_83(pbox_1_out_83), .in_84(pbox_1_out_84),
    .in_85(pbox_1_out_85), .in_86(pbox_1_out_86), .in_87(pbox_1_out_87), .in_88(pbox_1_out_88),
    .in_89(pbox_1_out_89), .in_90(pbox_1_out_90), .in_91(pbox_1_out_91), .in_92(pbox_1_out_92),
    .in_93(pbox_1_out_93), .in_94(pbox_1_out_94), .in_95(pbox_1_out_95), .in_96(pbox_1_out_96),
    .in_97(pbox_1_out_97), .in_98(pbox_1_out_98), .in_99(pbox_1_out_99), .in_100(pbox_1_out_100),
    .in_101(pbox_1_out_101), .in_102(pbox_1_out_102), .in_103(pbox_1_out_103), .in_104(pbox_1_out_104),
    .in_105(pbox_1_out_105), .in_106(pbox_1_out_106), .in_107(pbox_1_out_107), .in_108(pbox_1_out_108),
    .in_109(pbox_1_out_109), .in_110(pbox_1_out_110), .in_111(pbox_1_out_111), .in_112(pbox_1_out_112),
    .in_113(pbox_1_out_113), .in_114(pbox_1_out_114), .in_115(pbox_1_out_115), .in_116(pbox_1_out_116),
    .in_117(pbox_1_out_117), .in_118(pbox_1_out_118), .in_119(pbox_1_out_119), .in_120(pbox_1_out_120),
    .in_121(pbox_1_out_121), .in_122(pbox_1_out_122), .in_123(pbox_1_out_123), .in_124(pbox_1_out_124),
    .in_125(pbox_1_out_125), .in_126(pbox_1_out_126), .in_127(pbox_1_out_127), .in_128(pbox_1_out_128),
    .out_129(out_129), .out_130(out_130), .out_131(out_131), .out_132(out_132), .out_133(out_133),
    .out_134(out_134), .out_135(out_135), .out_136(out_136), .out_137(out_137), .out_138(out_138),
    .out_139(out_139), .out_140(out_140), .out_141(out_141), .out_142(out_142), .out_143(out_143),
    .out_144(out_144), .out_145(out_145), .out_146(out_146), .out_147(out_147), .out_148(out_148),
    .out_149(out_149), .out_150(out_150), .out_151(out_151), .out_152(out_152), .out_153(out_153),
    .out_154(out_154), .out_155(out_155), .out_156(out_156), .out_157(out_157), .out_158(out_158),
    .out_159(out_159), .out_160(out_160), .out_161(out_161), .out_162(out_162), .out_163(out_163),
    .out_164(out_164), .out_165(out_165), .out_166(out_166), .out_167(out_167), .out_168(out_168),
    .out_169(out_169), .out_170(out_170), .out_171(out_171), .out_172(out_172), .out_173(out_173),
    .out_174(out_174), .out_175(out_175), .out_176(out_176), .out_177(out_177), .out_178(out_178),
    .out_179(out_179), .out_180(out_180), .out_181(out_181), .out_182(out_182), .out_183(out_183),
    .out_184(out_184), .out_185(out_185), .out_186(out_186), .out_187(out_187), .out_188(out_188),
    .out_189(out_189), .out_190(out_190), .out_191(out_191), .out_192(out_192));
endmodule

module KeyTransform (
  input  in_1,
  input  in_2,
  input  in_3,
  input  in_4,
  input  in_5,
  input  in_6,
  input  in_7,
  input  in_8,
  input  in_9,
  input  in_10,
  input  in_11,
  input  in_12,
  input  in_13,
  input  in_14,
  input  in_15,
  input  in_16,
  input  in_17,
  input  in_18,
  input  in_19,
  input  in_20,
  input  in_21,
  input  in_22,
  input  in_23,
  input  in_24,
  input  in_25,
  input  in_26,
  input  in_27,
  input  in_28,
  input  in_29,
  input  in_30,
  input  in_31,
  input  in_32,
  input  in_33,
  input  in_34,
  input  in_35,
  input  in_36,
  input  in_37,
  input  in_38,
  input  in_39,
  input  in_40,
  input  in_41,
  input  in_42,
  input  in_43,
  input  in_44,
  input  in_45,
  input  in_46,
  input  in_47,
  input  in_48,
  input  in_49,
  input  in_50,
  input  in_51,
  input  in_52,
  input  in_53,
  input  in_54,
  input  in_55,
  input  in_56,
  input  in_57,
  input  in_58,
  input  in_59,
  input  in_60,
  input  in_61,
  input  in_62,
  input  in_63,
  input  in_64,
  input  in_65,
  input  in_66,
  input  in_67,
  input  in_68,
  input  in_69,
  input  in_70,
  input  in_71,
  input  in_72,
  input  in_73,
  input  in_74,
  input  in_75,
  input  in_76,
  input  in_77,
  input  in_78,
  input  in_79,
  input  in_80
);

  wire keytransformstep1_1_out_81, keytransformstep1_1_out_82, keytransformstep1_1_out_83,
       keytransformstep1_1_out_84, keytransformstep1_1_out_140, keytransformstep1_1_out_141,
       keytransformstep1_1_out_142, keytransformstep1_1_out_143, keytransformstep1_1_out_144,
       sbox4bit_1_out_5, sbox4bit_1_out_6, sbox4bit_1_out_7, sbox4bit_1_out_8;

  KeyTransformStep1 keytransformstep1_1 (
    .in_1(in_1), .in_2(in_2), .in_3(in_3), .in_4(in_4), .in_5(in_5), .in_6(in_6), .in_7(in_7), .in_8(in_8),
    .in_9(in_9), .in_10(in_10), .in_11(in_11), .in_12(in_12), .in_13(in_13), .in_14(in_14), .in_15(in_15),
    .in_16(in_16), .in_17(in_17), .in_18(in_18), .in_19(in_19), .in_20(in_20), .in_21(in_21), .in_22(in_22),
    .in_23(in_23), .in_24(in_24), .in_25(in_25), .in_26(in_26), .in_27(in_27), .in_28(in_28), .in_29(in_29),
    .in_30(in_30), .in_31(in_31), .in_32(in_32), .in_33(in_33), .in_34(in_34), .in_35(in_35), .in_36(in_36),
    .in_37(in_37), .in_38(in_38), .in_39(in_39), .in_40(in_40), .in_41(in_41), .in_42(in_42), .in_43(in_43),
    .in_44(in_44), .in_45(in_45), .in_46(in_46), .in_47(in_47), .in_48(in_48), .in_49(in_49), .in_50(in_50),
    .in_51(in_51), .in_52(in_52), .in_53(in_53), .in_54(in_54), .in_55(in_55), .in_56(in_56), .in_57(in_57),
    .in_58(in_58), .in_59(in_59), .in_60(in_60), .in_61(in_61), .in_62(in_62), .in_63(in_63), .in_64(in_64),
    .in_65(in_65), .in_66(in_66), .in_67(in_67), .in_68(in_68), .in_69(in_69), .in_70(in_70), .in_71(in_71),
    .in_72(in_72), .in_73(in_73), .in_74(in_74), .in_75(in_75), .in_76(in_76), .in_77(in_77), .in_78(in_78),
    .in_79(in_79), .in_80(in_80), .out_81(keytransformstep1_1_out_81), .out_82(keytransformstep1_1_out_82),
    .out_83(keytransformstep1_1_out_83), .out_84(keytransformstep1_1_out_84),
    .out_140(keytransformstep1_1_out_140), .out_141(keytransformstep1_1_out_141),
    .out_142(keytransformstep1_1_out_142), .out_143(keytransformstep1_1_out_143),
    .out_144(keytransformstep1_1_out_144));  // open: out_85, out_86, out_87, out_88, out_89, out_90, out_91, out_92, out_93, out_94, out_95, out_96, out_97, out_98, out_99, out_100, out_101, out_102, out_103, out_104, out_105, out_106, out_107, out_108, out_109, out_110, out_111, out_112, out_113, out_114, out_115, out_116, out_117, out_118, out_119, out_120, out_121, out_122, out_123, out_124, out_125, out_126, out_127, out_128, out_129, out_130, out_131, out_132, out_133, out_134, out_135, out_136, out_137, out_138, out_139, out_145, out_146, out_147, out_148, out_149, out_150, out_151, out_152, out_153, out_154, out_155, out_156, out_157, out_158, out_159, out_160
  SBox4Bit sbox4bit_1 (
    .in_1(keytransformstep1_1_out_81), .in_2(keytransformstep1_1_out_82), .in_3(keytransformstep1_1_out_83),
    .in_4(keytransformstep1_1_out_84), .out_5(sbox4bit_1_out_5), .out_6(sbox4bit_1_out_6),
    .out_7(sbox4bit_1_out_7), .out_8(sbox4bit_1_out_8));
  XOR5 xor5_1 (
    .in_1(keytransformstep1_1_out_140), .in_2(keytransformstep1_1_out_141),
    .in_3(keytransformstep1_1_out_142), .in_4(keytransformstep1_1_out_143), .in_5(keytransformstep1_1_out_144));  // open: in_6, in_7, in_8, in_9, in_10, out_11, out_12, out_13, out_14, out_15
endmodule

module KeyTransformStep1 (
  input  in_1,
  input  in_2,
  input  in_3,
  input  in_4,
  input  in_5,
  input  in_6,
  input  in_7,
  input  in_8,
  input  in_9,
  input  in_10,
  input  in_11,
  input  in_12,
  input  in_13,
  input  in_14,
  input  in_15,
  input  in_16,
  input  in_17,
  input  in_18,
  input  in_19,
  input  in_20,
  input  in_21,
  input  in_22,
  input  in_23,
  input  in_24,
  input  in_25,
  input  in_26,
  input  in_27,
  input  in_28,
  input  in_29,
  input  in_30,
  input  in_31,
  input  in_32,
  input  in_33,
  input  in_34,
  input  in_35,
  input  in_36,
  input  in_37,
  input  in_38,
  input  in_39,
  input  in_40,
  input  in_41,
  input  in_42,
  input  in_43,
  input  in_44,
  input  in_45,
  input  in_46,
  input  in_47,
  input  in_48,
  input  in_49,
  input  in_50,
  input  in_51,
  input  in_52,
  input  in_53,
  input  in_54,
  input  in_55,
  input  in_56,
  input  in_57,
  input  in_58,
  input  in_59,
  input  in_60,
  input  in_61,
  input  in_62,
  input  in_63,
  input  in_64,
  input  in_65,
  input  in_66,
  input  in_67,
  input  in_68,
  input  in_69,
  input  in_70,
  input  in_71,
  input  in_72,
  input  in_73,
  input  in_74,
  input  in_75,
  input  in_76,
  input  in_77,
  input  in_78,
  input  in_79,
  input  in_80,
  output out_81,
  output out_82,
  output out_83,
  output out_84,
  output out_85,
  output out_86,
  output out_87,
  output out_88,
  output out_89,
  output out_90,
  output out_91,
  output out_92,
  output out_93,
  output out_94,
  output out_95,
  output out_96,
  output out_97,
  output out_98,
  output out_99,
  output out_100,
  output out_101,
  output out_102,
  output out_103,
  output out_104,
  output out_105,
  output out_106,
  output out_107,
  output out_108,
  output out_109,
  output out_110,
  output out_111,
  output out_112,
  output out_113,
  output out_114,
  output out_115,
  output out_116,
  output out_117,
  output out_118,
  output out_119,
  output out_120,
  output out_121,
  output out_122,
  output out_123,
  output out_124,
  output out_125,
  output out_126,
  output out_127,
  output out_128,
  output out_129,
  output out_130,
  output out_131,
  output out_132,
  output out_133,
  output out_134,
  output out_135,
  output out_136,
  output out_137,
  output out_138,
  output out_139,
  output out_140,
  output out_141,
  output out_142,
  output out_143,
  output out_144,
  output out_145,
  output out_146,
  output out_147,
  output out_148,
  output out_149,
  output out_150,
  output out_151,
  output out_152,
  output out_153,
  output out_154,
  output out_155,
  output out_156,
  output out_157,
  output out_158,
  output out_159,
  output out_160
);


  assign out_81 = in_62;
  assign out_82 = in_63;
  assign out_83 = in_64;
  assign out_84 = in_65;
  assign out_85 = in_66;
  assign out_86 = in_67;
  assign out_87 = in_68;
  assign out_88 = in_69;
  assign out_89 = in_70;
  assign out_90 = in_71;
  assign out_91 = in_72;
  assign out_92 = in_73;
  assign out_93 = in_74;
  assign out_94 = in_75;
  assign out_95 = in_76;
  assign out_96 = in_77;
  assign out_97 = in_78;
  assign out_98 = in_79;
  assign out_99 = in_80;
  assign out_100 = in_1;
  assign out_101 = in_2;
  assign out_102 = in_3;
  assign out_103 = in_4;
  assign out_104 = in_5;
  assign out_105 = in_6;
  assign out_106 = in_7;
  assign out_107 = in_8;
  assign out_108 = in_9;
  assign out_109 = in_10;
  assign out_110 = in_11;
  assign out_111 = in_12;
  assign out_112 = in_13;
  assign out_113 = in_14;
  assign out_114 = in_15;
  assign out_115 = in_16;
  assign out_116 = in_17;
  assign out_117 = in_18;
  assign out_118 = in_19;
  assign out_119 = in_20;
  assign out_120 = in_21;
  assign out_121 = in_22;
  assign out_122 = in_23;
  assign out_123 = in_24;
  assign out_124 = in_25;
  assign out_125 = in_26;
  assign out_126 = in_27;
  assign out_127 = in_28;
  assign out_128 = in_29;
  assign out_129 = in_30;
  assign out_130 = in_31;
  assign out_131 = in_32;
  assign out_132 = in_33;
  assign out_133 = in_34;
  assign out_134 = in_35;
  assign out_135 = in_36;
  assign out_136 = in_37;
  assign out_137 = in_38;
  assign out_138 = in_39;
  assign out_139 = in_40;
  assign out_140 = in_41;
  assign out_141 = in_42;
  assign out_142 = in_43;
  assign out_143 = in_44;
  assign out_144 = in_45;
  assign out_145 = in_46;
  assign out_146 = in_47;
  assign out_147 = in_48;
  assign out_148 = in_49;
  assign out_149 = in_50;
  assign out_150 = in_51;
  assign out_151 = in_52;
  assign out_152 = in_53;
  assign out_153 = in_54;
  assign out_154 = in_55;
  assign out_155 = in_56;
  assign out_156 = in_57;
  assign out_157 = in_58;
  assign out_158 = in_59;
  assign out_159 = in_60;
  assign out_160 = in_61;
endmodule

module XOR5 (
  input  in_1,
  input  in_2,
  input  in_3,
  input  in_4,
  input  in_5,
  input  in_6,
  input  in_7,
  input  in_8,
  input  in_9,
  input  in_10,
  output out_11,
  output out_12,
  output out_13,
  output out_14,
  output out_15
);

  xor xor_1 (out_11, in_1, in_6);
  xor xor_2 (out_12, in_2, in_7);
  xor xor_3 (out_13, in_3, in_8);
  xor xor_4 (out_14, in_4, in_9);
  xor xor_5 (out_15, in_5, in_10);
endmodule

module Split4 (
  input  [3:0] in_1
);
endmodule
